# Fritzing sketch sistemperairan (saved by Fritzing 0.9.3b)
breadboards: 1

parts:
  U3 = ESP32S-HiLetgo [part_number=ESP32S-HiLetgo]
  Mod3 = KY-019 5V Relay Module [package="Breakout board"]
  VCC5 = Battery block 9V
  VCC6 = Battery
  ZS-042_RTC2 = ZS-042 RTC Module
  WATER_PUMP2 = water pump/motor  # not connected
  Mod4 = KY-019 5V Relay Module [package="Breakout board"]
  WATER_PUMP3 = water pump/motor  # not connected
  VCC7 = Battery block 9V
  J2 = Basic Servo
  M1 = PH meter with sensor in breadboard [package=THT]
  Part3 = SRF05 Ultrasonic Rangefinder

nets:
  VCC: U3.3.3, Mod3.+, ZS-042_RTC2.VCC, Mod4.+, J2.vcc, M1.pin2, Part3.VCC
  N1: U3.GPIO34, M1.pin1
  GND: U3.GND, Mod3.-, VCC6.-, ZS-042_RTC2.GND, Mod4.-, J2.gnd, M1.pin3, Part3.GND
  N2: U3.GPIO15, Mod3.S
  N3: U3.GPIO2, Mod4.S
  N4: U3.GPIO16, Part3.Trig
  N5: U3.GPIO17, Part3.Echo
  N6: U3.GPIO1, ZS-042_RTC2.SDA
  N7: U3.GPIO22, ZS-042_RTC2.SCL
  N8: Mod3.NO, VCC5.+
  N9: Mod4.NO, VCC7.+

custom parts:
  ESP32S-HiLetgo: HiLetgo ESP-WROOM-32 ESP32 ESP-32S Development Board 2.4GHz Dual-Mode WiFi + Bluetooth Dual Cores Microcontroller The ESP32 integrated with Antenna switches, RF Balun, power amplifiers, low-noise amplifiers, filters, and management modules, and the entire solution occupies the least area of PCB. 2.4 GHz Wi-Fi plus Bluetooth dual-mode chip, with TSMC Ultra-low power consumption 40nm technology,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
  KY-019 5V Relay Module: KY-019 5V Relay module, used to control AC circuits. (Special thanks to vanepp for fixing the PCB holes and other errors)
  water pump/motor: WATER PUMP BY ARDUBLOCKTR
  PH meter with sensor in breadboard: DFrobot PH meter (SKU SEN0161)
