# Fritzing sketch sistempertanian (saved by Fritzing 0.9.3b)
breadboards: 1

parts:
  U1 = ESP32S-HiLetgo [part_number=ESP32S-HiLetgo]
  DHT1 = Humidity and Temperature Sensor DHT11
  WATER_PUMP1 = water pump/motor  # not connected
  Mod1 = KY-019 5V Relay Module [package="Breakout board"]
  VCC1 = Battery
  VCC2 = Battery block 9V
  A1 = tds-sensor-meter-v1.0_1

nets:
  N1: U1.3.3, DHT1.Vcc, Mod1.+, A1.pin2
  N2: U1.GPIO34, A1.pin1
  N3: U1.GPIO25, DHT1.Data-signal
  N4: U1.GND, DHT1.GND_1, Mod1.-, VCC1.-, A1.pin3
  N5: U1.GPIO15, Mod1.S
  N6: Mod1.NO, VCC2.+

custom parts:
  ESP32S-HiLetgo: HiLetgo ESP-WROOM-32 ESP32 ESP-32S Development Board 2.4GHz Dual-Mode WiFi + Bluetooth Dual Cores Microcontroller The ESP32 integrated with Antenna switches, RF Balun, power amplifiers, low-noise amplifiers, filters, and management modules, and the entire solution occupies the least area of PCB. 2.4 GHz Wi-Fi plus Bluetooth dual-mode chip, with TSMC Ultra-low power consumption 40nm technology,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
  Humidity and Temperature Sensor DHT11: Digital relative humidity & temperature sensor DHT11
  water pump/motor: WATER PUMP BY ARDUBLOCKTR
  KY-019 5V Relay Module: KY-019 5V Relay module, used to control AC circuits. (Special thanks to vanepp for fixing the PCB holes and other errors)
  : TDS Meter V1.0 Development Board Water Meter Filter Measuring Water Sensor Module.
