# Fritzing sketch sistempeternakan (saved by Fritzing 0.9.3b)
breadboards: 1

parts:
  U2 = ESP32S-HiLetgo [part_number=ESP32S-HiLetgo]
  Mod2 = KY-019 5V Relay Module [package="Breakout board"]
  VCC3 = Battery block 9V
  VCC4 = Battery
  F1 = Fan - Ventilador [package=THT]
  Part1 = MQ-3 breakout
  ZS-042_RTC1 = ZS-042 RTC Module
  J1 = Basic Servo
  DHT2 = Humidity and Temperature Sensor DHT11

nets:
  VCC: U2.3.3, Mod2.+, Part1.VCC, ZS-042_RTC1.VCC, J1.vcc, DHT2.Vcc
  N1: U2.GPIO34, DHT2.Data-signal
  N2: U2.GPIO25, Part1.AO
  GND: U2.GND, Mod2.-, VCC4.-, Part1.GND, ZS-042_RTC1.GND, J1.gnd, DHT2.GND_1
  N3: U2.GPIO15, Mod2.S
  N4: U2.GPIO1, ZS-042_RTC1.SDA
  N5: U2.GPIO22, ZS-042_RTC1.SCL
  N6: Mod2.Common, F1.5V
  N7: Mod2.NO, VCC3.+
  N8: VCC3.-, F1.GND

custom parts:
  ESP32S-HiLetgo: HiLetgo ESP-WROOM-32 ESP32 ESP-32S Development Board 2.4GHz Dual-Mode WiFi + Bluetooth Dual Cores Microcontroller The ESP32 integrated with Antenna switches, RF Balun, power amplifiers, low-noise amplifiers, filters, and management modules, and the entire solution occupies the least area of PCB. 2.4 GHz Wi-Fi plus Bluetooth dual-mode chip, with TSMC Ultra-low power consumption 40nm technology,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
  KY-019 5V Relay Module: KY-019 5V Relay module, used to control AC circuits. (Special thanks to vanepp for fixing the PCB holes and other errors)
  Fan - Ventilador: Ventilador de 2 pines, se encuentra comunmente en computadoras de escritorio
  MQ-3 breakout: Alcohol sensor is capable of detecting alcohol (ethanol) particles on itself and gives the information in digital form back to us to manipulate with it. SKU:101251 • Voltage: 5V DC • Power: max 750mW • Measurement range: 0.04-4mg/L
  Humidity and Temperature Sensor DHT11: Digital relative humidity & temperature sensor DHT11
